# Fritzing sketch Smart Room Controller Fritzing (saved by Fritzing 0.9.4)
breadboards: 1

parts:
  Teensy_3_5 = Teensy 3.1
  Part2 = 12 NeoPixel Ring [part_number=1643]  # not connected
  U2 = ENCODER_RGB [package=encoder_led_2]  # not connected
  OLED_I2C2 = OLED 128x64 I2C Monochrome Display
  M2 = BMP280
  Part3 = Adafruit MicroSD card breakout board [part_number="Adafruit #254"]  # not connected
  WIZ820io2 = WIZ820io [part_number=WIZ820io]  # not connected
  Part4 = Adafruit MAX4466 Electret Microphone Amplifier [part_number="Adafruit #1063"]  # not connected

nets:
  GND: Teensy_3_5.GND, OLED_I2C2.GND
  N1: Teensy_3_5.A4/D18, OLED_I2C2.SDA
  N2: Teensy_3_5.A5/D19, OLED_I2C2.SCK
  3V3: Teensy_3_5.3V3, OLED_I2C2.VDD, M2.VIN

custom parts:
  12 NeoPixel Ring: 12 ultra bright smart LED NeoPixels are arranged in a circle with 1.5" (37mm) outer diameter. The rings are 'chainable' - connect the output pin of one to the input pin of another. Use only one microcontroller pin to control as many as you can chain together! Each LED is addressable as the driver chip is inside the LED. Each one has ~18mA constant current drive so the color will be very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
  ENCODER_RGB: SparkFun RGB rotary Encoder
  BMP280: Temperature Humidity Barometric presure Sensor, I2C
  Adafruit MicroSD card breakout board: Not just a simple breakout board, this microSD adapter goes the extra mile - designed for ease of use. Onboard 5v->3v regulator provides 150mA for power-hungry cards 3v level shifting means you can use this with ease on either 3v or 5v systems Uses a proper level shifting chip, not resistors: less problems, and faster read/write access Use 3 or 4 digital pins to read and write 2Gb+ of storage!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
  Adafruit MAX4466 Electret Microphone Amplifier: Add an ear to your project with this well-designed electret microphone amplifier. This fully assembled and tested board comes with a 20-20KHz electret microphone soldered on. For the amplification, we use the Maxim MAX4466, an op-amp specifically designed for this delicate task! The amplifier has excellent power supply noise rejection, so this amplifier sounds really good and isn't nearly as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
